# Fritzing sketch circuitDesign (saved by Fritzing 1.0.4)
breadboards: 1

parts:
  Part1 = Black Joystick KY-023
  S1 = Pushbutton [package="[SMD]"]
  R2 = TRIMPOT [maximum_resistance=10kΩ knob_status=50% power=0.5W package=3386u]
  Mod1 = ESP32-TTGO-T-DISPLAY

nets:
  N1: Part1.SW, Mod1.33
  N2: Part1.VRy, Mod1.32
  N3: Part1.VRx, Mod1.39
  N4: Part1.+5V, R2.CW, Mod1.3V
  N5: Part1.GND, S1.Pin_1, S1.Pin_2, R2.CCW, Mod1.G-1, Mod1.G-2, Mod1.G-10, Mod1.G-11, Mod1.G-14
  N6: S1.Pin_3, S1.Pin_4, Mod1.15
  N7: R2.WIPER, Mod1.13

custom parts:
  Black Joystick KY-023: Description: The joystick is a combination of 2 analoog potentiometer and a digital switch. Arduino GND --> Module pin - Arduino +5V --> Module pin +5V Arduino Analoog 0 --> Module VRx Arduino Analoog 1 --> Module VRy Arduino Digital --> Module SW Dimensions: 1" x 1.25"
  ESP32-TTGO-T-DISPLAY: LILYGO TTGO T-Display GD32VF103CBT6 Main Chip ST7789 1.14 Inch IPS 240x135 Resolution Minimalist Development Board.
